# Fritzing sketch dht11LCDnewWIRING2buttonsREMOTE (saved by Fritzing 0.9.3b)
breadboards: 1

parts:
  Part1 = Arduino Uno (Rev3)
  S1 = Momentary Switch [package=ksa_sealed_tac_switch]
  DHT1 = DHT11 Humitidy and Temperature Sensor
  R1 = Resistor [tolerance=±5% resistance=10k package="0402 [SMD]"]
  D1 = Diode [package=diode-hv]
  C1 = Electrolytic Capacitor [capacitance=10µF voltage=63V package="200 mil [THT, electrolytic]"]
  Part2 = LCD1602-I2C
  U1 = 2-Channel 5v Relay Shield [package=relay-2ch5v10a]
  C2 = Electrolytic Capacitor [capacitance=10µF voltage=63V package="200 mil [THT, electrolytic]"]
  S2 = Momentary Switch [package=ksa_sealed_tac_switch]
  R2 = Resistor [tolerance=±5% resistance=10k package="0402 [SMD]"]
  D2 = Diode [package=diode-hv]
  InfraRedsensor = TSOP312.., 314.. [package=THT]
  R3 = Resistor [tolerance=±5% resistance=1k package="0402 [SMD]"]
  C3 = Electrolytic Capacitor [capacitance=4.7µF voltage=63V package="200 mil [THT, electrolytic]"]

nets:
  N1: Part1.A4/SDA, Part2.SDA
  N2: Part1.A5/SCL, Part2.SCL
  N3: Part1.D9_PWM, DHT1.NULL
  N4: Part1.D11_PWM/MOSI, InfraRedsensor.Data
  N5: Part1.D2, D2.C
  N6: Part1.D3_PWM, D1.C
  N7: Part1.D7, U1.IN1
  N8: Part1.3V3, R3.Pin_1
  VCC: Part1.5V, S1.1, DHT1.DATA, Part2.VCC, U1.VCC, S2.1
  GND: Part1.GND, DHT1.GND, R1.Pin_0, C1.-, Part2.GND, U1.GND, C2.-, R2.Pin_0, InfraRedsensor.GND, C3.-
  N9: S1.3, R1.Pin_1
  N10: S1.4, D1.A, C1.+
  N11: C2.+, S2.4, D2.A
  N12: S2.3, R2.Pin_1
  N13: InfraRedsensor.Vs, R3.Pin_0, C3.+

notes:
  The Capacitors for the push buttons can be 1uF 63 Volts also, instead of 10uF 63 Volts. Different values give different debounce effect to the push buttons.

custom parts:
  DHT11 Humitidy and Temperature Sensor: DHT11 Humidity and Temperature Sensor
  LCD1602-I2C: A standard character display, usually with 2x16 characters. Comes in many colors with LCM1602 IIC attached.
  2-Channel 5v Relay Shield: 2 Channel 5v Relay Shield w. 2x SPD-06VDC-SD-C
